// Logisim project 14_paridade_impar.circ as structural Verilog: 1 circuit, main circuit paridade_impar
module paridade_impar (
  input  A,
  input  B,
  input  C,
  input  P,
  output Pc
);

  wire xor_1_out, xor_2_out, xor_3_out;

  xor xor_1 (xor_1_out, A, B);
  xor xor_2 (xor_2_out, C, P);
  not not_1 (Pc, xor_3_out);
  xor xor_3 (xor_3_out, xor_1_out, xor_2_out);
endmodule
