// Logisim project 15_KARNAUGH.circ as structural Verilog: 2 circuits, main circuit circuito_original
module circuito_original (
  input  A,
  input  B,
  input  C,
  input  A_2,
  input  B_2,
  input  C_2,
  input  A_3,
  input  B_3,
  input  C_3,
  output S
);

  wire and_1_out, and_2_out, and_3_out, not_1_out, not_2_out, not_3_out, or_1_out;

  not not_1 (not_1_out, A);
  not not_2 (not_2_out, C);
  not not_3 (not_3_out, A_2);
  and and_1 (and_1_out, not_1_out, B, not_2_out);
  and and_2 (and_2_out, not_3_out, B_2, C_2);
  and and_3 (and_3_out, A_3, B_3, C_3);
  or or_1 (or_1_out, and_1_out, and_2_out);
  or or_2 (S, or_1_out, and_3_out);
endmodule

module circuito_otimizado (
  input  A,
  input  B,
  input  B_2,
  input  C,
  output S
);

  wire and_1_out, and_2_out, not_1_out;

  not not_1 (not_1_out, A);
  and and_1 (and_1_out, not_1_out, B);
  and and_2 (and_2_out, B_2, C);
  or or_1 (S, and_1_out, and_2_out);
endmodule
