// Logisim project 17_detector_primos.circ as structural Verilog: 1 circuit, main circuit primos
module primos (
  input  A,
  input  B,
  input  C,
  input  D,
  output out_5
);

  wire and_1_out, and_2_out, nand_1_out, not_1_out, or_1_out, or_2_out;

  not not_1 (not_1_out, A);
  or or_1 (or_1_out, not_1_out, B);
  nand nand_1 (nand_1_out, B, A);
  or or_2 (or_2_out, C, or_1_out);
  and and_1 (and_1_out, C, nand_1_out);
  and and_2 (and_2_out, D, or_2_out);
  or or_3 (out_5, and_2_out, and_1_out);
endmodule
