// Logisim project 1_FLIPFLOP_JK.circ as structural Verilog: 1 circuit, main circuit main
module main (
  input  J,
  input  K,
  input  SET,
  input  CLEAR,
  input  SET_2,
  input  J_2,
  input  Q,
  input  CLEAR_2,
  output \SAÍDA ,
  output out_10,
  output Q_2,
  output nQ
);

  wire clock_2_out, CLOCK_out, nand_1_out, nand_2_out, nand_3_out, nand_4_out, nand_5_out, nand_6_out,
       not_1_out, not_2_out, not_3_out;

  Clock CLOCK (.out(CLOCK_out));
  J_K_Flip_Flop j_k_ff_1 (
    .J(J), .clk(CLOCK_out), .K(K), .Q(\SAÍDA ), .Qn(out_10), .preset(SET), .reset(CLEAR));  // open: en
  Clock clock_2 (.out(clock_2_out));
  not not_1 (not_1_out, clock_2_out);
  nand nand_1 (nand_1_out, nQ, J_2, clock_2_out);
  nand nand_2 (nand_2_out, clock_2_out, Q, Q_2);
  not not_2 (not_2_out, SET_2);
  not not_3 (not_3_out, CLEAR_2);
  nand nand_3 (nand_3_out, not_2_out, nand_1_out, nand_1_out, nand_4_out);
  nand nand_4 (nand_4_out, nand_3_out, nand_2_out, not_3_out);
  nand nand_5 (nand_5_out, not_3_out, nand_3_out, not_1_out);
  nand nand_6 (nand_6_out, not_1_out, nand_4_out, not_2_out);
  nand nand_7 (Q_2, not_2_out, nand_5_out, nQ);
  nand nand_8 (nQ, Q_2, nand_6_out, not_3_out);
endmodule
