// Logisim project 4_Somador_8bits_4.circ as structural Verilog: 3 circuits, main circuit somador_1bit
module somador_1bit (
  input  CIN,
  input  A,
  input  B,
  output S,
  output COUT
);

  wire and_1_out, and_2_out, xor_1_out;

  xor xor_1 (xor_1_out, A, B);
  and and_1 (and_1_out, A, B);
  xor xor_2 (S, CIN, xor_1_out);
  and and_2 (and_2_out, CIN, xor_1_out);
  or or_1 (COUT, and_2_out, and_1_out);
endmodule

module somador_4bits (
  input  CIN,
  input  A0,
  input  B0,
  input  A1,
  input  B1,
  input  A2,
  input  B2,
  input  A3,
  input  B3,
  output S1,
  output S2,
  output S3,
  output S4,
  output COUT
);

  wire somador_1bit_1_cout, somador_1bit_2_cout, SOMADOR_DE_1_BIT_cout;

  somador_1bit SOMADOR_DE_1_BIT (.CIN(CIN), .A(A0), .B(B0), .S(S1), .COUT(SOMADOR_DE_1_BIT_cout));
  somador_1bit somador_1bit_1 (.CIN(SOMADOR_DE_1_BIT_cout), .A(A1), .B(B1), .S(S2), .COUT(somador_1bit_1_cout));
  somador_1bit somador_1bit_2 (.CIN(somador_1bit_1_cout), .A(A2), .B(B2), .S(S3), .COUT(somador_1bit_2_cout));
  somador_1bit somador_1bit_3 (.CIN(somador_1bit_2_cout), .A(A3), .B(B3), .S(S4), .COUT(COUT));
endmodule

module somador_8bits (
  input  CIN,
  input  A0,
  input  BO,
  input  A1,
  input  B1,
  input  A2,
  input  B2,
  input  A3,
  input  B3,
  input  A4,
  input  B4,
  input  A5,
  input  B5,
  input  A6,
  input  A7,
  input  B7,
  output COUT
);

  wire SOMADOR_DE_4_BITS_cout;
  wire [3:0] somador_4bits_1_s1, SOMADOR_DE_4_BITS_s1;

  somador_4bits SOMADOR_DE_4_BITS (
    .CIN(CIN), .A0(A0), .B0(BO), .A1(A1), .B1(B1), .A2(A2), .B2(B2), .A3(A3), .B3(B3),
    .S1(SOMADOR_DE_4_BITS_s1[0]), .S2(SOMADOR_DE_4_BITS_s1[1]), .S3(SOMADOR_DE_4_BITS_s1[2]),
    .S4(SOMADOR_DE_4_BITS_s1[3]), .COUT(SOMADOR_DE_4_BITS_cout));
  somador_4bits somador_4bits_1 (
    .CIN(SOMADOR_DE_4_BITS_cout), .A0(A4), .B0(B4), .A1(A5), .B1(B5), .A2(A6), .B2(1'b1), .A3(A7), .B3(B7),
    .S1(somador_4bits_1_s1[0]), .S2(somador_4bits_1_s1[1]), .S3(somador_4bits_1_s1[2]),
    .S4(somador_4bits_1_s1[3]), .COUT(COUT));
  Hex_Digit_Display hex_digit_display_1 (.value(somador_4bits_1_s1));  // open: dp
  Hex_Digit_Display hex_digit_display_2 (.value(SOMADOR_DE_4_BITS_s1));  // open: dp
endmodule
