// Logisim project 9_det_sequencia.circ as structural Verilog: 1 circuit, main circuit det_sequencia
module det_sequencia (
  input  in_1,
  output OUT
);

  wire A_q, A_qn, and_1_out, and_2_out, and_3_out, and_4_out, B_q, B_qn, clock_1_out, or_1_out, or_2_out;

  and and_1 (and_1_out, ~in_1, A_q, B_q);  // AND_Gate
  and and_2 (and_2_out, in_1, A_qn);
  and and_3 (and_3_out, in_1, B_qn);
  and and_4 (and_4_out, in_1, A_q);
  or or_1 (or_1_out, and_1_out, and_2_out, and_3_out);
  or or_2 (or_2_out, and_4_out, B_q);
  Clock clock_1 (.out(clock_1_out));
  D_Flip_Flop A (.clk(clock_1_out), .D(or_2_out), .Q(A_q), .Qn(A_qn));  // open: preset, en, reset
  D_Flip_Flop B (.clk(clock_1_out), .D(or_1_out), .Q(B_q), .Qn(B_qn));  // open: preset, en, reset
  and and_5 (OUT, ~in_1, A_q, B_q);  // AND_Gate
endmodule
