// Logisim project Contador_sincrono.circ as structural Verilog: 1 circuit, main circuit contador_sincrono
module contador_sincrono (
  output [3:0] CONTADOR
);

  wire and_1_out, and_2_out, CLOCK_out;

  Clock CLOCK (.out(CLOCK_out));
  J_K_Flip_Flop j_k_ff_1 (.J(1'b1), .clk(CLOCK_out), .K(1'b1), .Q(CONTADOR[0]));  // open: Qn, preset, en, reset
  J_K_Flip_Flop j_k_ff_2 (
    .J(CONTADOR[0]), .clk(CLOCK_out), .K(CONTADOR[0]), .Q(CONTADOR[1]));  // open: Qn, preset, en, reset
  and and_1 (and_1_out, CONTADOR[0], CONTADOR[1]);
  J_K_Flip_Flop j_k_ff_3 (
    .J(and_1_out), .clk(CLOCK_out), .K(and_1_out), .Q(CONTADOR[2]));  // open: Qn, preset, en, reset
  and and_2 (and_2_out, CONTADOR[2], CONTADOR[1], CONTADOR[0]);
  J_K_Flip_Flop j_k_ff_4 (
    .J(and_2_out), .clk(CLOCK_out), .K(and_2_out), .Q(CONTADOR[3]));  // open: Qn, preset, en, reset
endmodule
