// Logisim project FLIPFLOP_D.circ as structural Verilog: 1 circuit, main circuit main
module main (
  input  D,
  output Q,
  output nQ
);

  wire clock_out, nand_1_out, nand_2_out, nand_3_out, nand_4_out, nand_5_out, nand_6_out, not_1_out,
       not_2_out;

  Clock clock (.out(clock_out));
  not not_1 (not_1_out, D);
  nand nand_1 (nand_1_out, D, clock_out);
  not not_2 (not_2_out, clock_out);
  nand nand_2 (nand_2_out, clock_out, not_1_out);
  nand nand_3 (nand_3_out, nand_1_out, nand_1_out, nand_4_out);
  nand nand_4 (nand_4_out, nand_3_out, nand_2_out);
  nand nand_5 (nand_5_out, nand_3_out, not_2_out);
  nand nand_6 (nand_6_out, nand_5_out, not_2_out, nand_4_out);
  nand nand_7 (Q, nand_5_out, nQ);
  nand nand_8 (nQ, Q, nand_6_out);
endmodule
