// Logisim project MemoriaRAM.circ as structural Verilog: 2 circuits, main circuit memoria_ram
module valor (
  input  CLK,
  input  [7:0] ENTRADA,
  input  clear,
  output [7:0] SAIDA
);

  wire [7:0] multiplexer_1_out;

  Multiplexer #(.width(8)) multiplexer_1 (
    .in0(ENTRADA), .in1({8{1'b0}}), .out(multiplexer_1_out), .sel(clear));  // open: en
  D_Flip_Flop d_ff_1 (.clk(CLK), .D(multiplexer_1_out[0]), .Q(SAIDA[0]));  // open: Qn, preset, en, reset
  D_Flip_Flop d_ff_2 (.clk(CLK), .D(multiplexer_1_out[1]), .Q(SAIDA[1]));  // open: Qn, preset, en, reset
  D_Flip_Flop d_ff_3 (.clk(CLK), .D(multiplexer_1_out[2]), .Q(SAIDA[2]));  // open: Qn, preset, en, reset
  D_Flip_Flop d_ff_4 (.clk(CLK), .D(multiplexer_1_out[3]), .Q(SAIDA[3]));  // open: Qn, preset, en, reset
  D_Flip_Flop d_ff_5 (.clk(CLK), .D(multiplexer_1_out[4]), .Q(SAIDA[4]));  // open: Qn, preset, en, reset
  D_Flip_Flop d_ff_6 (.clk(CLK), .D(multiplexer_1_out[5]), .Q(SAIDA[5]));  // open: Qn, preset, en, reset
  D_Flip_Flop d_ff_7 (.clk(CLK), .D(multiplexer_1_out[6]), .Q(SAIDA[6]));  // open: Qn, preset, en, reset
  D_Flip_Flop d_ff_8 (.clk(CLK), .D(multiplexer_1_out[7]), .Q(SAIDA[7]));  // open: Qn, preset, en, reset
endmodule

module memoria_ram (
  input  [7:0] ENTRADA,
  input  [2:0] seletor,
  input  clear,
  output [7:0] SAIDA
);

  wire CLK_out, demultiplexer_1_out0, demultiplexer_1_out1, demultiplexer_1_out2, demultiplexer_1_out3,
       demultiplexer_1_out4, demultiplexer_1_out5, demultiplexer_1_out6, demultiplexer_1_out7;
  wire [7:0] demultiplexer_2_out0, demultiplexer_2_out1, demultiplexer_2_out2, demultiplexer_2_out3,
       demultiplexer_2_out4, demultiplexer_2_out5, demultiplexer_2_out6, demultiplexer_2_out7, valor_1_saida,
       valor_2_saida, valor_3_saida, valor_4_saida, valor_5_saida, valor_6_saida, valor_7_saida,
       valor_8_saida;

  Clock CLK (.out(CLK_out));
  Demultiplexer #(.select(3)) demultiplexer_1 (
    .out0(demultiplexer_1_out0), .out1(demultiplexer_1_out1), .out2(demultiplexer_1_out2),
    .out3(demultiplexer_1_out3), .out4(demultiplexer_1_out4), .out5(demultiplexer_1_out5),
    .out6(demultiplexer_1_out6), .out7(demultiplexer_1_out7), .in(CLK_out), .sel(seletor));  // open: en
  Demultiplexer #(.select(3), .width(8)) demultiplexer_2 (
    .out0(demultiplexer_2_out0), .out1(demultiplexer_2_out1), .out2(demultiplexer_2_out2),
    .out3(demultiplexer_2_out3), .out4(demultiplexer_2_out4), .out5(demultiplexer_2_out5),
    .out6(demultiplexer_2_out6), .out7(demultiplexer_2_out7), .in(ENTRADA), .sel(seletor));  // open: en
  valor valor_1 (.ENTRADA(demultiplexer_2_out0), .SAIDA(valor_1_saida), .CLK(demultiplexer_1_out0), .clear(clear));
  valor valor_2 (.ENTRADA(demultiplexer_2_out1), .SAIDA(valor_2_saida), .CLK(demultiplexer_1_out1), .clear(clear));
  valor valor_3 (.ENTRADA(demultiplexer_2_out2), .SAIDA(valor_3_saida), .CLK(demultiplexer_1_out2), .clear(clear));
  valor valor_4 (.ENTRADA(demultiplexer_2_out3), .SAIDA(valor_4_saida), .CLK(demultiplexer_1_out3), .clear(clear));
  valor valor_5 (.ENTRADA(demultiplexer_2_out4), .SAIDA(valor_5_saida), .CLK(demultiplexer_1_out4), .clear(clear));
  valor valor_6 (.ENTRADA(demultiplexer_2_out5), .SAIDA(valor_6_saida), .CLK(demultiplexer_1_out5), .clear(clear));
  valor valor_7 (.ENTRADA(demultiplexer_2_out6), .SAIDA(valor_7_saida), .CLK(demultiplexer_1_out6), .clear(clear));
  valor valor_8 (.ENTRADA(demultiplexer_2_out7), .SAIDA(valor_8_saida), .CLK(demultiplexer_1_out7), .clear(clear));
  Multiplexer #(.select(3), .width(8)) multiplexer_1 (
    .in0(valor_1_saida), .in1(valor_2_saida), .in2(valor_3_saida), .in3(valor_4_saida), .in4(valor_5_saida),
    .in5(valor_6_saida), .in6(valor_7_saida), .in7(valor_8_saida), .out(SAIDA), .sel(seletor));  // open: en
endmodule
