// Logisim project Somador_8bits_4.circ as structural Verilog: 2 circuits, main circuit somador_8_bits
module somador_8_bits (
  input  [7:0] ENTRADA_A,
  output [7:0] \SAÍDA ,
  output OVERFLOW
);

  wire adicao_1_carry_out, adicao_2_carry_out, adicao_3_carry_out, adicao_4_carry_out, adicao_5_carry_out,
       adicao_6_carry_out, adicao_7_carry_out;

  adicao adicao_1 (.S(\SAÍDA [0]), .CARRY_OUT(adicao_1_carry_out), .A(ENTRADA_A[0]), .B(1'b0), .CARRY_IN(1'b0));
  adicao adicao_2 (
    .S(\SAÍDA [1]), .CARRY_OUT(adicao_2_carry_out), .A(ENTRADA_A[1]), .B(1'b0), .CARRY_IN(adicao_1_carry_out));
  adicao adicao_3 (
    .S(\SAÍDA [2]), .CARRY_OUT(adicao_3_carry_out), .A(ENTRADA_A[2]), .B(1'b1), .CARRY_IN(adicao_2_carry_out));
  adicao adicao_4 (
    .S(\SAÍDA [3]), .CARRY_OUT(adicao_4_carry_out), .A(ENTRADA_A[3]), .B(1'b0), .CARRY_IN(adicao_3_carry_out));
  adicao adicao_5 (
    .S(\SAÍDA [4]), .CARRY_OUT(adicao_5_carry_out), .A(ENTRADA_A[4]), .B(1'b0), .CARRY_IN(adicao_4_carry_out));
  adicao adicao_6 (
    .S(\SAÍDA [5]), .CARRY_OUT(adicao_6_carry_out), .A(ENTRADA_A[5]), .B(1'b0), .CARRY_IN(adicao_5_carry_out));
  adicao adicao_7 (
    .S(\SAÍDA [6]), .CARRY_OUT(adicao_7_carry_out), .A(ENTRADA_A[6]), .B(1'b0), .CARRY_IN(adicao_6_carry_out));
  adicao adicao_8 (.S(\SAÍDA [7]), .CARRY_OUT(OVERFLOW), .A(ENTRADA_A[7]), .B(1'b0), .CARRY_IN(adicao_7_carry_out));
endmodule

module adicao (
  input  A,
  input  B,
  input  CARRY_IN,
  output S,
  output CARRY_OUT
);

  wire and_1_out, and_2_out, xor_1_out;

  xor xor_1 (xor_1_out, A, B);
  xor xor_2 (S, xor_1_out, CARRY_IN);
  and and_1 (and_1_out, CARRY_IN, xor_1_out);
  and and_2 (and_2_out, B, A);
  or or_1 (CARRY_OUT, and_1_out, and_2_out);
endmodule
