// Logisim project ULA_8_BITS.circ as structural Verilog: 1 circuit, main circuit ULA_8BITS
module ULA_8BITS (
  input  [7:0] ENTRADA_A,
  input  [7:0] ENTRADA_B,
  input  [7:0] shift,
  input  [3:0] seletor,
  output [7:0] \saída 
);

  wire [7:0] and_1_out, nand_1_out, nor_1_out, not_1_out, or_1_out, shift_2_1_left, shift_2_1_right,
       somador_8_bits_1_saida, \subtrator_1_saída , xor_1_out;

  assign or_1_out = ENTRADA_A | ENTRADA_B;  // OR_Gate or_1, 8 bits wide
  assign and_1_out = ENTRADA_A & ENTRADA_B;  // AND_Gate and_1, 8 bits wide
  assign not_1_out = ~ENTRADA_A;  // NOT_Gate not_1, 8 bits wide
  assign xor_1_out = ENTRADA_A ^ ENTRADA_B;  // XOR_Gate xor_1, 8 bits wide
  somador_8_bits somador_8_bits_1 (
    .ENTRADA_A(ENTRADA_B), .ENTRADA_B(ENTRADA_A), .SAIDA(somador_8_bits_1_saida));  // open: OVERFLOW
  shift_2 shift_2_1 (.entrada(shift), .LEFT(shift_2_1_left), .RIGHT(shift_2_1_right));
  subtrator subtrator_1 (.\SAÍDA (\subtrator_1_saída ), .A(ENTRADA_A), .B(ENTRADA_B));  // open: OVERFLOW
  assign nor_1_out = ~(ENTRADA_A | ENTRADA_B);  // NOR_Gate nor_1, 8 bits wide
  assign nand_1_out = ~(ENTRADA_A & ENTRADA_B);  // NAND_Gate nand_1, 8 bits wide
  Multiplexer #(.select(4), .width(8)) multiplexer_1 (
    .in1(or_1_out), .in2(and_1_out), .in3(not_1_out), .in4(nor_1_out), .in5(nand_1_out), .in6(xor_1_out),
    .in7(somador_8_bits_1_saida), .in8(shift_2_1_left), .in9(shift_2_1_right), .in10(\subtrator_1_saída ),
    .out(\saída ), .sel(seletor));  // open: in0, in11, in12, in13, in14, in15, en

  // Notes on the sheet:
  //   SOM
  //   SUB
  //   OR
  //   AND
  //   NOT(A)
  //   NOR
  //   NAND
  //   XOR
  //   SOMADOR
  //   SHIFT ESQUERDA
  //   SHIFT DIRETIA
  //   SUB
  //   0001
  //   0010
  //   0011
  //   0100
  //   0101
  //   0110
  //   0111
  //   1000
  //   1001
  //   1010
endmodule
