// Logisim project banco_registradores.circ as structural Verilog: 2 circuits, main circuit Registrador
module Registrador (
  input  in_1,
  input  [7:0] in_2,
  output [7:0] out_3
);

  D_Flip_Flop d_ff_1 (.clk(in_1), .D(in_2[7]), .Q(out_3[7]));  // open: Qn, preset, en, reset
  D_Flip_Flop d_ff_2 (.clk(in_1), .D(in_2[6]), .Q(out_3[6]));  // open: Qn, preset, en, reset
  D_Flip_Flop d_ff_3 (.clk(in_1), .D(in_2[5]), .Q(out_3[5]));  // open: Qn, preset, en, reset
  D_Flip_Flop d_ff_4 (.clk(in_1), .D(in_2[4]), .Q(out_3[4]));  // open: Qn, preset, en, reset
  D_Flip_Flop d_ff_5 (.clk(in_1), .D(in_2[3]), .Q(out_3[3]));  // open: Qn, preset, en, reset
  D_Flip_Flop d_ff_6 (.clk(in_1), .D(in_2[2]), .Q(out_3[2]));  // open: Qn, preset, en, reset
  D_Flip_Flop d_ff_7 (.clk(in_1), .D(in_2[1]), .Q(out_3[1]));  // open: Qn, preset, en, reset
  D_Flip_Flop d_ff_8 (.clk(in_1), .D(in_2[0]), .Q(out_3[0]));  // open: Qn, preset, en, reset
endmodule

module Banco_de_registradores (
  input  [7:0] in_1,
  input  [1:0] in_2,
  output [7:0] out_3,
  output [7:0] out_4,
  output [7:0] out_5,
  output [7:0] out_6
);

  wire and_1_out, and_2_out, and_3_out, and_4_out, and_5_out, and_6_out, and_7_out, and_8_out, clock_1_out,
       not_1_out, not_2_out, not_3_out, not_4_out;

  not not_1 (not_1_out, in_2[1]);
  not not_2 (not_2_out, in_2[0]);
  not not_3 (not_3_out, in_2[1]);
  not not_4 (not_4_out, in_2[0]);
  and and_1 (and_1_out, not_1_out, not_2_out);
  and and_2 (and_2_out, not_3_out, in_2[0], in_2[0]);
  and and_3 (and_3_out, in_2[1], not_4_out);
  and and_4 (and_4_out, in_2[1], in_2[0]);
  Clock clock_1 (.out(clock_1_out));
  and and_5 (and_5_out, clock_1_out, and_1_out);
  and and_6 (and_6_out, clock_1_out, and_2_out);
  and and_7 (and_7_out, clock_1_out, and_3_out);
  and and_8 (and_8_out, and_4_out, clock_1_out);
  Registrador registrador_1 (.in_2(in_1), .out_3(out_3), .in_1(and_5_out));
  Registrador registrador_2 (.in_2(in_1), .out_3(out_4), .in_1(and_6_out));
  Registrador registrador_3 (.in_2(in_1), .out_3(out_5), .in_1(and_7_out));
  Registrador registrador_4 (.in_2(in_1), .out_3(out_6), .in_1(and_8_out));
endmodule
