// Logisim project decod_7seg.circ as structural Verilog: 8 circuits, main circuit dec_7seg
// a
module seg_a (
  input  [3:0] entrada,
  output saida_A
);

  wire and_1_out, and_2_out, and_3_out, and_4_out, and_5_out, and_6_out;

  and and_1 (and_1_out, ~entrada[2], ~entrada[0]);  // AND_Gate
  and and_2 (and_2_out, ~entrada[3], entrada[1]);  // AND_Gate
  and and_3 (and_3_out, ~entrada[3], entrada[2], entrada[0]);  // AND_Gate
  and and_4 (and_4_out, entrada[2], entrada[1]);
  and and_5 (and_5_out, entrada[3], ~entrada[0]);  // AND_Gate
  and and_6 (and_6_out, entrada[3], ~entrada[2], ~entrada[1]);  // AND_Gate
  or or_1 (saida_A, and_1_out, and_2_out, and_3_out, and_4_out, and_5_out, and_6_out);
endmodule

// b
module seg_b (
  input  [3:0] entrada,
  output \saída 
);

  wire and_1_out, and_2_out, and_3_out, and_4_out, and_5_out;

  and and_1 (and_1_out, entrada[3], ~entrada[1], entrada[0]);  // AND_Gate
  and and_2 (and_2_out, ~entrada[2], ~entrada[0]);  // AND_Gate
  and and_3 (and_3_out, ~entrada[3], ~entrada[1], ~entrada[0]);  // AND_Gate
  and and_4 (and_4_out, ~entrada[3], entrada[1], entrada[0]);  // AND_Gate
  and and_5 (and_5_out, ~entrada[3], ~entrada[2]);  // AND_Gate
  or or_1 (\saída , and_1_out, and_2_out, and_3_out, and_4_out, and_5_out);
endmodule

// c
module seg_c (
  input  [3:0] entrada,
  output seg_C
);

  wire and_1_out, and_2_out, and_3_out, and_4_out, and_5_out;

  and and_1 (and_1_out, ~entrada[1], entrada[0]);  // AND_Gate
  and and_2 (and_2_out, ~entrada[3], entrada[2]);  // AND_Gate
  and and_3 (and_3_out, entrada[3], ~entrada[2]);  // AND_Gate
  and and_4 (and_4_out, ~entrada[3], ~entrada[1]);  // AND_Gate
  and and_5 (and_5_out, ~entrada[3], entrada[0]);  // AND_Gate
  or or_1 (seg_C, and_1_out, and_2_out, and_3_out, and_4_out, and_5_out);
endmodule

// d
module seg_d (
  input  [3:0] entrada,
  output seg_d
);

  wire and_1_out, and_2_out, and_3_out, and_4_out, and_5_out;

  and and_1 (and_1_out, entrada[2], ~entrada[1], entrada[0]);  // AND_Gate
  and and_2 (and_2_out, ~entrada[2], entrada[1], entrada[0]);  // AND_Gate
  and and_3 (and_3_out, entrada[2], entrada[1], ~entrada[0]);  // AND_Gate
  and and_4 (and_4_out, entrada[3], ~entrada[1]);  // AND_Gate
  and and_5 (and_5_out, ~entrada[3], ~entrada[2], ~entrada[0]);  // AND_Gate
  or or_1 (seg_d, and_1_out, and_2_out, and_3_out, and_4_out, and_5_out);
endmodule

// e
module seg_e (
  input  [3:0] entrada,
  output seg_e
);

  wire and_1_out, and_2_out, and_3_out, and_4_out;

  and and_1 (and_1_out, ~entrada[2], ~entrada[0]);  // AND_Gate
  and and_2 (and_2_out, entrada[1], ~entrada[0]);  // AND_Gate
  and and_3 (and_3_out, entrada[3], entrada[1]);
  and and_4 (and_4_out, entrada[3], entrada[2]);
  or or_1 (seg_e, and_1_out, and_2_out, and_3_out, and_4_out);
endmodule

// f
module seg_f (
  input  [3:0] entrada,
  output seg_f
);

  wire and_1_out, and_2_out, and_3_out, and_4_out, and_5_out;

  and and_1 (and_1_out, ~entrada[1], ~entrada[0]);  // AND_Gate
  and and_2 (and_2_out, entrada[2], ~entrada[0]);  // AND_Gate
  and and_3 (and_3_out, ~entrada[3], entrada[2], ~entrada[1]);  // AND_Gate
  and and_4 (and_4_out, entrada[3], ~entrada[2]);  // AND_Gate
  and and_5 (and_5_out, entrada[3], entrada[1]);
  or or_1 (seg_f, and_1_out, and_2_out, and_3_out, and_4_out, and_5_out);
endmodule

// g
module seg_g (
  input  [3:0] entrada,
  output seg_g
);

  wire and_1_out, and_2_out, and_3_out, and_4_out, and_5_out;

  and and_1 (and_1_out, ~entrada[2], entrada[1]);  // AND_Gate
  and and_2 (and_2_out, entrada[3], ~entrada[2]);  // AND_Gate
  and and_3 (and_3_out, entrada[3], entrada[0]);
  and and_4 (and_4_out, entrada[1], ~entrada[0]);  // AND_Gate
  and and_5 (and_5_out, ~entrada[3], entrada[2], ~entrada[1]);  // AND_Gate
  or or_1 (seg_g, and_1_out, and_2_out, and_3_out, and_4_out, and_5_out);
endmodule

module dec_7seg (
  input  [3:0] ENTRADA
);

  wire seg_a_1_saida_a, \seg_b_1_saída , seg_c_1_seg_c, seg_d_1_seg_d, seg_e_1_seg_e, seg_f_1_seg_f,
       seg_g_1_seg_g;

  seg_a seg_a_1 (.saida_A(seg_a_1_saida_a), .entrada(ENTRADA));
  seg_b seg_b_1 (.\saída (\seg_b_1_saída ), .entrada(ENTRADA));
  seg_c seg_c_1 (.seg_C(seg_c_1_seg_c), .entrada(ENTRADA));
  seg_d seg_d_1 (.seg_d(seg_d_1_seg_d), .entrada(ENTRADA));
  seg_e seg_e_1 (.seg_e(seg_e_1_seg_e), .entrada(ENTRADA));
  seg_f seg_f_1 (.seg_f(seg_f_1_seg_f), .entrada(ENTRADA));
  seg_g seg_g_1 (.seg_g(seg_g_1_seg_g), .entrada(ENTRADA));
  _7_Segment_Display u_7_segment_display_1 (
    .g(seg_g_1_seg_g), .f(seg_f_1_seg_f), .a(seg_a_1_saida_a), .b(\seg_b_1_saída ), .e(seg_e_1_seg_e),
    .d(seg_d_1_seg_d), .c(seg_c_1_seg_c));  // open: dp
endmodule
