// Logisim project det_sequencia.circ as structural Verilog: 1 circuit, main circuit detector_sequencia_101
module detector_sequencia_101 (
  input  ENTRADA,
  output S
);

  wire and_1_out, CLK_out, d_ff_1_q, d_ff_2_q, not_1_out;

  Clock CLK (.out(CLK_out));
  D_Flip_Flop d_ff_1 (.clk(CLK_out), .D(ENTRADA), .Q(d_ff_1_q));  // open: Qn, preset, en, reset
  not not_1 (not_1_out, ENTRADA);
  D_Flip_Flop d_ff_2 (.clk(CLK_out), .D(and_1_out), .Q(d_ff_2_q));  // open: Qn, preset, en, reset
  and and_1 (and_1_out, d_ff_1_q, not_1_out);
  and and_2 (S, d_ff_2_q, ENTRADA);
endmodule
