// Logisim project detector_numero_primo.circ as structural Verilog: 1 circuit, main circuit detector_num_primo
module detector_num_primo (
  input  [3:0] ENTRADA,
  output S
);

  wire and_1_out, and_2_out, and_3_out, and_4_out;

  and and_1 (and_1_out, ~ENTRADA[3], ~ENTRADA[2], ENTRADA[1]);  // AND_Gate
  and and_2 (and_2_out, ENTRADA[2], ~ENTRADA[1], ENTRADA[0]);  // AND_Gate
  and and_3 (and_3_out, ~ENTRADA[2], ENTRADA[1], ENTRADA[0]);  // AND_Gate
  and and_4 (and_4_out, ~ENTRADA[3], ENTRADA[2], ENTRADA[0]);  // AND_Gate
  or or_1 (S, and_1_out, and_2_out, and_3_out, and_4_out);
endmodule
