// Logisim project extensor_de_sinal.circ as structural Verilog: 1 circuit, main circuit extensor
module extensor (
  input  [3:0] ENTRADA,
  output [7:0] \SAÍDA 
);


  assign \SAÍDA  = {{5{ENTRADA[3]}}, ENTRADA[2:0]};
endmodule
