// Logisim project maq_estados.circ as structural Verilog: 1 circuit, main circuit maq_estados
module maq_estados (
  input  ENTRADA,
  output \SAÍDA 
);

  wire and_1_out, and_2_out, CLK_out, or_1_out;

  and and_1 (and_1_out, ~\SAÍDA , ENTRADA);  // AND_Gate
  and and_2 (and_2_out, \SAÍDA , ~ENTRADA);  // AND_Gate
  Clock CLK (.out(CLK_out));
  or or_1 (or_1_out, and_1_out, and_2_out);
  D_Flip_Flop ESTADO_ATUAL (.clk(CLK_out), .D(or_1_out), .Q(\SAÍDA ));  // open: Qn, preset, en, reset
endmodule
