// Logisim project mux_4x1.circ as structural Verilog: 1 circuit, main circuit main
module main (
  input  i0,
  input  i1,
  input  i2,
  input  i3,
  input  S1,
  input  S0,
  output out_7
);

  wire and_1_out, and_2_out, and_3_out, and_4_out, not_1_out, not_2_out, not_3_out;

  not not_1 (not_1_out, S1);
  not not_2 (not_2_out, S0);
  not not_3 (not_3_out, S0);
  and and_1 (and_1_out, i0, not_1_out, not_2_out);
  and and_2 (and_2_out, i1, not_1_out, S0);
  and and_3 (and_3_out, i2, S1, not_3_out);
  and and_4 (and_4_out, i3, S1, S0);
  or or_1 (out_7, and_1_out, and_2_out, and_3_out, and_4_out);
endmodule
