// Logisim project otimizacao_logica.circ as structural Verilog: 2 circuits, main circuit original
module original (
  input  A,
  input  B,
  output out_3
);

  wire and_1_out, and_2_out, not_1_out, not_2_out;

  not not_1 (not_1_out, B);
  not not_2 (not_2_out, A);
  and and_1 (and_1_out, A, not_1_out);
  and and_2 (and_2_out, not_2_out, B);
  or or_1 (out_3, and_1_out, and_2_out);
endmodule

module otimizado (
  input  A,
  input  B,
  output out_3
);

  xor xor_1 (out_3, A, B);
endmodule
