// Logisim project shift.circ as structural Verilog: 1 circuit, main circuit shift_2
module shift_2 (
  input  [7:0] ENTRADA,
  output [7:0] ESQUERDA,
  output [7:0] DIREITA
);


  assign DIREITA = {3'b000, ENTRADA[7:3]};
  assign ESQUERDA = {ENTRADA[4:0], 3'b000};
endmodule
