// Logisim project somador_8_bits.circ as structural Verilog: 2 circuits, main circuit somador_8_bits
module somador_8_bits (
  input  [7:0] ENTRADA_A,
  input  [7:0] ENTRADA_B,
  output [7:0] SAIDA,
  output OVERFLOW
);

  wire adicao_1_carry_out, adicao_2_carry_out, adicao_3_carry_out, adicao_4_carry_out, adicao_5_carry_out,
       adicao_6_carry_out, adicao_7_carry_out;

  adicao adicao_1 (.S(SAIDA[0]), .CARRY_OUT(adicao_1_carry_out), .A(ENTRADA_A[0]), .B(ENTRADA_B[0]), .CARRY_IN(1'b0));
  adicao adicao_2 (
    .S(SAIDA[1]), .CARRY_OUT(adicao_2_carry_out), .A(ENTRADA_A[1]), .B(ENTRADA_B[1]),
    .CARRY_IN(adicao_1_carry_out));
  adicao adicao_3 (
    .S(SAIDA[2]), .CARRY_OUT(adicao_3_carry_out), .A(ENTRADA_A[2]), .B(ENTRADA_B[2]),
    .CARRY_IN(adicao_2_carry_out));
  adicao adicao_4 (
    .S(SAIDA[3]), .CARRY_OUT(adicao_4_carry_out), .A(ENTRADA_A[3]), .B(ENTRADA_B[3]),
    .CARRY_IN(adicao_3_carry_out));
  adicao adicao_5 (
    .S(SAIDA[4]), .CARRY_OUT(adicao_5_carry_out), .A(ENTRADA_A[4]), .B(ENTRADA_B[4]),
    .CARRY_IN(adicao_4_carry_out));
  adicao adicao_6 (
    .S(SAIDA[5]), .CARRY_OUT(adicao_6_carry_out), .A(ENTRADA_A[5]), .B(ENTRADA_B[5]),
    .CARRY_IN(adicao_5_carry_out));
  adicao adicao_7 (
    .S(SAIDA[6]), .CARRY_OUT(adicao_7_carry_out), .A(ENTRADA_A[6]), .B(ENTRADA_B[6]),
    .CARRY_IN(adicao_6_carry_out));
  adicao adicao_8 (
    .S(SAIDA[7]), .CARRY_OUT(OVERFLOW), .A(ENTRADA_A[7]), .B(ENTRADA_B[7]), .CARRY_IN(adicao_7_carry_out));
endmodule

module adicao (
  input  A,
  input  B,
  input  CARRY_IN,
  output S,
  output CARRY_OUT
);

  wire and_1_out, and_2_out, xor_1_out;

  xor xor_1 (xor_1_out, A, B);
  xor xor_2 (S, xor_1_out, CARRY_IN);
  and and_1 (and_1_out, CARRY_IN, xor_1_out);
  and and_2 (and_2_out, B, A);
  or or_1 (CARRY_OUT, and_1_out, and_2_out);
endmodule
